# Fritzing sketch wiring (saved by Fritzing 0.9.1b)
breadboards: 1

parts:
  LED1 = RGB LED (com. cathode, rgb) [package="5 mm [THT]"]
  Part1 = Arduino Uno (Rev3)

nets:
  N1: LED1.red_anode, Part1.D3_PWM
  N2: LED1.common_cathode, Part1.5V
  N3: LED1.green_anode, Part1.D5_PWM
  N4: LED1.blue_anode, Part1.D6_PWM
